# Fritzing sketch servosketch (saved by Fritzing 0.9.3b)

parts:
  Part2 = Arduino Uno (Rev3) - ICSP
  J2 = Basic Servo
  U1 = POT [package=pot_mammoth]
  U2 = POT [package=pot_mammoth]
  J1 = Basic Servo

nets:
  N1: Part2.A0, U1.A
  N2: Part2.A1, U2.A
  N3: Part2.D9_PWM, J2.pulse
  N4: Part2.D10_PWM/SS, J1.pulse
  VCC: Part2.5V, J2.vcc, U1.E, U2.E, J1.vcc
  GND: Part2.GND, J2.gnd, U1.S, U2.S, J1.gnd
