# Fritzing sketch antenna (saved by Fritzing 0.9.3b)
breadboards: 1

parts:
  Part1 = Arduino Uno (Rev3) - ICSP
  ANT1 = Antenna
  R1 = Resistor [tolerance=±5% resistance=220 package="2512 [SMD]"]
  C1 = Tantalum Capacitor [capacitance="1 μF" package="A 3216 [SMD, tantalum]"]

nets:
  N1: Part1.A0, C1.+
  N2: Part1.GND, C1.-
  N3: ANT1.antenna_lead, R1.Pin_0
